# Fritzing sketch ftdi232 (saved by Fritzing 0.9.5d)

parts:
  Part2 = FTDI Basic Programmer
  WeMos_D1_Mini1 = WeMos D1 Mini

nets:
  N1: Part2.RXI, WeMos_D1_Mini1.TX
  N2: Part2.TXO, WeMos_D1_Mini1.RX
  N3: Part2.POWER, WeMos_D1_Mini1.3V3
  N4: Part2.GND, WeMos_D1_Mini1.G

notes:
  to Computer USB
